# Fritzing sketch ADS1115-DustSensor (saved by Fritzing 0.9.3b)
breadboards: 1

parts:
  U1 = Sharp Dust Sensor [part_number=GP2Y1010AU0F]
  W1 = ESPr Developer [package="DIP (Dual Inline) [THT]"]
  パーツ1 = Adafruit ADS1115 16Bit I2C ADC [part_number="Adafruit #1085"]
  8x2_I2C_LCD1 = LCD 8x2 Char I2C Display [package=DIP]
  C1 = Electrolytic Capacitor [capacitance=0.22mF package="200 mil [THT, electrolytic]"]
  R1 = Resistor [tolerance=±5% resistance=150 package=THT]
  パーツ2 = Adafruit BME280

nets:
  N1: U1.V-LED, C1.+, R1.Pin_0
  GND: U1.LED-GND, U1.S-GND, W1.GND, パーツ1.AIN1, パーツ1.ADDR, パーツ1.GND, 8x2_I2C_LCD1.GND, C1.-, パーツ2.GND, パーツ2.SDO/ADR
  N2: U1.LED, W1.IO14
  N3: U1.Vo, パーツ1.AIN0
  N4: U1.VCC, W1.VOUT, R1.Pin_1
  3.3V: W1.3V3, パーツ1.VDD, 8x2_I2C_LCD1.VCC, パーツ2.3.3V, パーツ2.CS
  N5: W1.IO4, パーツ1.SDA, 8x2_I2C_LCD1.SDA, パーツ2.SDI/SDA
  N6: W1.IO5, パーツ1.SCL, 8x2_I2C_LCD1.SCL, パーツ2.SCK/SCL

custom parts:
  Sharp Dust Sensor: Sharp GP2Y1010AU0F Dust Sensor
  Adafruit ADS1115 16Bit I2C ADC: For microcontrollers without an analog-to-digital converter or when you want a higher-precision ADC, the ADS1115 provides 16-bit precision at 860 samples/second over I2C. The chip can be configured as 4 single-ended input channels, or two differential channels. As a nice bonus, it even includes a programmable gain amplifier, up to x16, to help boost up smaller single/differential signals to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
  LCD 8x2 Char I2C Display: Switch Science / I2C 8x2 Char LCD Display
  Adafruit BME280: Bosch has stepped up their game with their new BME280 sensor, an environmental sensor with temperature, barometric pressure and humidity! This sensor is great for all sorts of weather/environmental sensing and can even be used in both I2C and SPI! This precision sensor from Bosch is the best low-cost sensing solution for measuring humidity with ±3% accuracy, barometric pressure with ±1 hPa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
